// Digital circuit A.dig as structural Verilog
module A (
  input  c,
  input  b,
  input  a,
  output z
);

  wire nand_1_out, or_1_out, or_2_out, xnor_1_out;

  nand nand_1 (nand_1_out, ~c, a);  // NAnd
  xnor xnor_1 (xnor_1_out, c, b);
  or or_1 (or_1_out, c, b);
  or or_2 (or_2_out, ~nand_1_out, a);  // Or
  and and_1 (z, or_2_out, xnor_1_out, or_1_out);
endmodule
