// Digital circuit A.dig as structural Verilog
module A (
  input  b,
  input  a,
  input  c,
  output z
);

  wire nand_1_out, or_1_out, or_2_out, xnor_1_out;

  xnor xnor_1 (xnor_1_out, b, c);
  nand nand_1 (nand_1_out, ~b, a);  // NAnd
  or or_1 (or_1_out, b, a);
  or or_2 (or_2_out, c, ~xnor_1_out);  // Or
  and and_1 (z, nand_1_out, or_1_out, or_2_out);
endmodule
