// Digital circuit A.dig as structural Verilog
module A (
  input  b,
  input  a,
  input  c,
  output z
);

  wire nand_1_out;

  nand nand_1 (nand_1_out, ~a, b);  // NAnd
  xnor xnor_1 (z, nand_1_out, ~b, c);  // XNOr
endmodule
