// Digital circuit A.dig as structural Verilog
module A (
  input  c,
  input  b,
  input  a,
  output z
);

  wire and_1_out, nand_1_out, or_1_out, xnor_1_out;

  xnor xnor_1 (xnor_1_out, a, c);
  nand nand_1 (nand_1_out, ~a, b);  // NAnd
  or or_1 (or_1_out, a, b);
  and and_1 (and_1_out, c, nand_1_out, or_1_out);
  or or_2 (z, ~xnor_1_out, and_1_out);  // Or
endmodule
